# Fritzing sketch wire (saved by Fritzing 0.9.9b)

parts:
  Mod1 = Raspberry Pi 4B  # not connected
  BAT1 = 12 battery [package=battery]
  Part1 = Arduino Mega ADK (Rev3)
  USBTTL1 = USB A Plug
  USBTTL2 = Micro USB B Plug
  JACK1 = 2.1mm Barrel Jack with Terminal Block
  M1 = DC Motor
  M2 = DC Motor
  M3 = DC Motor
  M4 = DC Motor
  L298N1 = L298N DC motor driver
  L298N2 = L298N DC motor driver
  IC1 = Rasberry Pi NIOR Camera [chip_label=IC package="DIP (Dual Inline) [THT]"]  # not connected
  Part2 = HC-SR501 Body Sensor Module
  T1 = LM35 Temperature Sensor [package="TO92 [THT]"]
  T2 = LM35 Temperature Sensor [package="TO92 [THT]"]
  T3 = LM35 Temperature Sensor [package="TO92 [THT]"]
  T4 = LM35 Temperature Sensor [package="TO92 [THT]"]
  T5 = LM35 Temperature Sensor [package="TO92 [THT]"]
  U1 = GAS_SENSOR [package=mq-3]
  U2 = GAS_SENSOR [package=mq-3]
  J1 = Basic Servo
  J2 = Basic Servo
  J3 = Basic Servo
  J4 = Basic Servo  # not connected
  J5 = Basic Servo
  J6 = Basic Servo
  PWM1 = PCA9685 16x12-bit PWM Breakout
  Part3 = Adafruit MAX4466 Electret Microphone Amplifier [part_number="Adafruit #1063"]
  HC-1 = HC-12 Module
  Antenna1 = HC-12 Antenna
  HC-SR04_Sensor_1 = HC-SR04 Ultrasonic Distance Sensor
  HC-SR04_Sensor_2 = HC-SR04 Ultrasonic Distance Sensor
  J7 = Basic Servo
  J8 = Basic Servo
  J9 = Basic Servo
  J10 = Basic Servo
  J11 = Basic Servo
  J12 = Basic Servo

nets:
  N1: BAT1.-, JACK1.NEG
  12V: BAT1.+, JACK1.POS, L298N1.12V, L298N2.12V
  N2: Part1.A0, PWM1.no_name_yet#504
  N3: Part1.A1, PWM1.no_name_yet#503
  GND: Part1.GND, L298N1.GND, L298N2.GND, Part2.GND, T1.GND, T2.GND, T3.GND, T4.GND, T5.GND, U1.H1, U2.H1, PWM1.no_name_yet#501, PWM1.no_name_yet#1000, PWM1.no_name_yet#1001, PWM1.no_name_yet#1002, PWM1.no_name_yet#1004, PWM1.no_name_yet#1006, PWM1.no_name_yet#1008, PWM1.no_name_yet#1009, PWM1.no_name_yet#1010, PWM1.no_name_yet#1013, Part3.GND, HC-1.GND, HC-SR04_Sensor_1.GND, HC-SR04_Sensor_2.GND
  N4: Part1.D13_PWM, L298N2.ENB
  N5: Part1.D12_PWM, L298N2.IN4
  N6: Part1.D11_PWM, L298N2.IN3
  N7: Part1.D10_PWM, L298N2.IN2
  N8: Part1.D9_PWM, L298N2.IN1
  N9: Part1.D8_PWM, L298N2.ENA
  VCC: Part1.5V, Part2.VCC, T1.+Vs, T2.+Vs, T3.+Vs, T4.+Vs, T5.+Vs, U1.H2, U2.H2, PWM1.no_name_yet#505, Part3.VCC, HC-1.VCC, HC-SR04_Sensor_1.VCC, HC-SR04_Sensor_2.VCC
  N10: Part1.D0/RX0, HC-1.RXD
  N11: Part1.D1/TX0, HC-1.TXD
  N12: Part1.D2_PWM, L298N1.ENA
  N13: Part1.D3_PWM, L298N1.IN1
  N14: Part1.D4_PWM, L298N1.IN2
  N15: Part1.D5_PWM, L298N1.IN3
  N16: Part1.D6_PWM, L298N1.IN4
  N17: Part1.D7_PWM, L298N1.ENB
  N18: Part1.D39, T1.Vout
  N19: Part1.D40, Part3.OUT
  N20: Part1.D41, T2.Vout
  N21: Part1.D42, HC-SR04_Sensor_2.ECHO
  N22: Part1.D43, T5.Vout
  N23: Part1.D44, HC-SR04_Sensor_2.TRIG
  N24: Part1.D45, T4.Vout
  N25: Part1.D46, HC-SR04_Sensor_1.ECHO
  N26: Part1.D47, T3.Vout
  N27: Part1.D48, Part2.OUT
  N28: Part1.D49, HC-SR04_Sensor_1.TRIG
  N29: USBTTL1.usb, USBTTL2.usb
  N30: M1.pin_1, L298N1.OUT1
  N31: M1.pin_2, L298N1.OUT2
  N32: M2.pin_1, L298N1.OUT3
  N33: M2.pin_2, L298N1.OUT4
  N34: M3.pin_1, L298N2.OUT1
  N35: M3.pin_2, L298N2.OUT2
  N36: M4.pin_1, L298N2.OUT3
  N37: M4.pin_2, L298N2.OUT4
  N38: J1.pulse, PWM1.no_name_yet#1
  N39: J2.pulse, PWM1.no_name_yet#0
  N40: J3.pulse, PWM1.no_name_yet#2
  N41: J5.pulse, PWM1.no_name_yet#9
  N42: J6.pulse, PWM1.no_name_yet#8
  N43: PWM1.no_name_yet#4, J8.pulse
  N44: PWM1.no_name_yet#5, J7.pulse
  N45: PWM1.no_name_yet#6, J9.pulse
  N46: PWM1.no_name_yet#11, J11.pulse
  N47: PWM1.no_name_yet#12, J10.pulse
  N48: PWM1.no_name_yet#13, J12.pulse
  N49: PWM1.no_name_yet#100, PWM1.no_name_yet#101, PWM1.no_name_yet#102, PWM1.no_name_yet#104, PWM1.no_name_yet#105, PWM1.no_name_yet#106, PWM1.no_name_yet#108, PWM1.no_name_yet#109, PWM1.no_name_yet#110, PWM1.no_name_yet#113
  N50: HC-1.ANT, Antenna1.ANT

custom parts:
  12 battery: 12V lead acid type battery, like the Husqvarna YTH2448 12V 35AH battery. This is the mini version 1/4 the size of the actual battery to be closer to typical breadboard parts (around 2in wide rathher than 7in). The pads in pcb are sized to accomidate up to 14ga wire (as these batterys will deliver high currents.)
  L298N DC motor driver: 2x DC motor driver with 78M05 positive voltage regulator (7..35 V) L298N: max 46 V, 2 A Set 5 V Enable jumper to enable 5 V regultor (needed for the L298N) and +5 V output at screw terminal or supply external +5 V at screw terminal Set ENA and/or ENB to +5 V to enable motor permanently or supply ENA and/or ENB with PWM signal IN1 and IN2 set rotation directory for motor A (OUT1/OUT2) IN2 and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
  Rasberry Pi NIOR Camera: Camera
  HC-SR501 Body Sensor Module: Pyroelectric Infrared PIR Motion Sensor Detector Module
  Adafruit MAX4466 Electret Microphone Amplifier: Add an ear to your project with this well-designed electret microphone amplifier. This fully assembled and tested board comes with a 20-20KHz electret microphone soldered on. For the amplification, we use the Maxim MAX4466, an op-amp specifically designed for this delicate task! The amplifier has excellent power supply noise rejection, so this amplifier sounds really good and isn't nearly as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
  HC-12 Module: HC-12 433Mhz Module
  HC-12 Antenna: Antenna for HC-12 433Mhz Module
